// Logisim project 4-Bit-Microprocessor.circ as structural Verilog: 9 circuits, main circuit main
module main (
);

  wire button_1_out, clock_1_out, mux_1_o0, mux_1_o1, mux_1_o2, mux_1_o3, register_file_1_out_11;
  wire [3:0] alu_1_o0, rom_1_data, rom_1_data_2;
  wire [6:0] register_file_1_out_12;
  wire [7:0] counter_1_q, rom_2_data;

  Clock clock_1 (.out(clock_1_out));
  Button button_1 (.out(button_1_out));
  Counter counter_1 (.Q(counter_1_q), .clk(clock_1_out), .clr(button_1_out));  // open: load, D, count, carry
  ROM rom_1 (.addr(counter_1_q), .data({rom_1_data_2, rom_1_data}));  // open: sel
  ROM #(.addrWidth(4)) rom_2 (.addr(rom_1_data_2), .data(rom_2_data));  // open: sel
  MUX mux_1 (
    .A0(rom_1_data[0]), .A1(rom_1_data[1]), .A2(rom_1_data[2]), .A3(rom_1_data[3]), .B0(alu_1_o0[0]),
    .B1(alu_1_o0[1]), .B2(alu_1_o0[2]), .B3(alu_1_o0[3]), .S0(rom_2_data[3]), .O0(mux_1_o0), .O1(mux_1_o1),
    .O2(mux_1_o2), .O3(mux_1_o3));
  Register_File register_file_1 (
    .A0(mux_1_o0), .A1(mux_1_o1), .A2(mux_1_o2), .A3(mux_1_o3), .WE(rom_2_data[0]), .S0(rom_2_data[1]),
    .in_6(clock_1_out), .out_8(register_file_1_out_12[4]), .out_9(register_file_1_out_12[5]),
    .out_10(register_file_1_out_12[6]), .out_11(register_file_1_out_11), .out_12(register_file_1_out_12[0]),
    .out_13(register_file_1_out_12[1]), .out_14(register_file_1_out_12[2]), .out_15(register_file_1_out_12[3]));
  ALU alu_1 (
    .in_1(rom_2_data[7]), .A0(register_file_1_out_12[4]), .A1(register_file_1_out_12[5]),
    .A2(register_file_1_out_12[6]), .A3(register_file_1_out_11), .B0(register_file_1_out_12[0]),
    .B1(register_file_1_out_12[1]), .B2(register_file_1_out_12[2]), .B3(register_file_1_out_12[3]),
    .S0(rom_2_data[5]), .S1(rom_2_data[6]), .Clock(clock_1_out), .WE(rom_2_data[4]), .O0(alu_1_o0[0]),
    .O1(alu_1_o0[1]), .O2(alu_1_o0[2]), .O3(alu_1_o0[3]));
  TTY tty_1 (.data(register_file_1_out_12), .clk(clock_1_out), .we(rom_2_data[2]), .clr(button_1_out));

  // Notes on the sheet:
  //   4-Bit-Microprocessor
  //   Binary Counter
  //   Clock
  //   Reset
  //   Program PROM
  //   Instruction Decoder
  //   contents of rom_1 (hex, n*v repeats v):
  //   18 24 30 15 26 30 1c 26 30 30 1f 26 30 1c 22 30 10 22 30 19 24 30 10 22 30 11 26 30 1d 26 30 10 22
  //   30 1e 24 30 11 24 30 1e 24 30 13 24 30 19 25 30 10 22 30 16 25 30 1f 24 30 12 25 30 11 24 30 1d 20
  //   30 12 25 30 1f 26 30 1c 26 30 30 10 22 30 1e 26 30 1f 26 30 1e 22 30 10 22 30 1a 23 30 10 22 30 12
  //   23 30 12 23 30 12 24 30 13 24 30 15 24 30 13 23 30 18 23 30 16 23 30 1d 20 30 13 25 30 15 26 30 1d
  //   26 30 10 22 30 1a 23 30 10 22 30 19 24 30 16 25 30 1d 20 30 15 23 30 1b 22 30 14 23 30 1d 23 30 15
  //   24 60 40 23 30 1d 20 30 12 23 30 1a 22 30 13 23 30 1d 23 30 12 22 60 40 60 40 23 30 1d 20 30 14 23
  //   30 1d 22 30 12 23 30 1d 23 30 12 2f 90 40 21 60 40 24 60 40 23 30 1d 20 30 14 23 30 1b 22 30 13 23
  //   30 1d 23 30 14 23 60 40 23 30 1d 20 30 12 24 30 19 25 30 15 24 30 11 22 30
  //   contents of rom_2 (hex, n*v repeats v):
  //   0 3 1 4 b a 10 30 50 70 90 c0
  //   MUX
  //   Register File
  //   ALU
  //   ASCII DISPLAY
endmodule

module ALU (
  input  in_1,
  input  A0,
  input  A1,
  input  A2,
  input  A3,
  input  B0,
  input  B1,
  input  B2,
  input  B3,
  input  S0,
  input  S1,
  input  Clock,
  input  WE,
  output O0,
  output O1,
  output O2,
  output O3
);

  wire bit_wise_and_1_p9, bit_wise_and_1_p10, bit_wise_and_1_p11, bit_wise_and_1_p12, bit_wise_or_1_p9,
       bit_wise_or_1_p10, bit_wise_or_1_p11, bit_wise_or_1_p12, bit_wise_xor_1_p9, bit_wise_xor_1_p10,
       bit_wise_xor_1_p11, bit_wise_xor_1_p12, four4_1_mux_1_p19, four4_1_mux_1_p20, four4_1_mux_1_p21,
       four4_1_mux_1_p22, n4_bit_add_sub_1_out_0, n4_bit_add_sub_1_out_1, n4_bit_add_sub_1_out_2,
       n4_bit_add_sub_1_out_3;

  _4_Bit_Add_Sub u_4_bit_add_sub_1 (
    .A0(A0), .A1(A1), .A2(A2), .A3(A3), .B0(B0), .B1(B1), .B2(B2), .B3(B3), .in_1(in_1),
    .OUT_0(n4_bit_add_sub_1_out_0), .OUT_1(n4_bit_add_sub_1_out_1), .OUT_2(n4_bit_add_sub_1_out_2),
    .OUT_3(n4_bit_add_sub_1_out_3));
  // bit_wise_OR bit_wise_or_1: pin names not known; wires that end beside it: A0, A1, A2, A3, B0, B1, B2, B3, bit_wise_or_1_p9, bit_wise_or_1_p10, bit_wise_or_1_p11, bit_wise_or_1_p12
  // bit_wise_AND bit_wise_and_1: pin names not known; wires that end beside it: A0, A1, A2, A3, B0, B1, B2, B3, bit_wise_and_1_p9, bit_wise_and_1_p10, bit_wise_and_1_p11, bit_wise_and_1_p12
  // bit_wise_XOR bit_wise_xor_1: pin names not known; wires that end beside it: A0, A1, A2, A3, B0, B1, B2, B3, bit_wise_xor_1_p9, bit_wise_xor_1_p10, bit_wise_xor_1_p11, bit_wise_xor_1_p12
  // Four4_1_MUX four4_1_mux_1: pin names not known; wires that end beside it: n4_bit_add_sub_1_out_0, n4_bit_add_sub_1_out_1, n4_bit_add_sub_1_out_2, n4_bit_add_sub_1_out_3, bit_wise_or_1_p9, bit_wise_or_1_p10, bit_wise_or_1_p11, bit_wise_or_1_p12, bit_wise_and_1_p9, bit_wise_and_1_p10, bit_wise_and_1_p11, bit_wise_and_1_p12, bit_wise_xor_1_p9, bit_wise_xor_1_p10, bit_wise_xor_1_p11, bit_wise_xor_1_p12, S0, S1, four4_1_mux_1_p19, four4_1_mux_1_p20, four4_1_mux_1_p21, four4_1_mux_1_p22
  _4_Bit_Register u_4_bit_register_1 (
    .A0(four4_1_mux_1_p19), .A1(four4_1_mux_1_p20), .A2(four4_1_mux_1_p21), .A3(four4_1_mux_1_p22),
    .Clock(Clock), .Load(WE), .out_7(O0), .out_8(O1), .out_9(O2), .out_10(O3));

  // Notes on the sheet:
  //   ALU
  //   Inputs
  //   ADD/SUB
  //   OR
  //   AND
  //   XOR
  //   4:1 MUX
  //   Selectors
  //   Accumulator
  //   Register Controls
  //   Outputs
endmodule

module MUX (
  input  A0,
  input  A1,
  input  A2,
  input  A3,
  input  B0,
  input  B1,
  input  B2,
  input  B3,
  input  S0,
  output O0,
  output O1,
  output O2,
  output O3
);

  wire and_1_out, and_2_out, and_3_out, and_4_out, and_5_out, and_6_out, and_7_out, and_8_out, not_1_out;

  not not_1 (not_1_out, S0);
  and and_1 (and_1_out, A0, not_1_out);
  and and_2 (and_2_out, A1, not_1_out);
  and and_3 (and_3_out, A2, not_1_out);
  and and_4 (and_4_out, A3, not_1_out);
  and and_5 (and_5_out, B0, S0);
  and and_6 (and_6_out, B1, S0);
  and and_7 (and_7_out, B2, S0);
  and and_8 (and_8_out, B3, S0);
  or or_1 (O0, and_1_out, and_5_out);
  or or_2 (O1, and_2_out, and_6_out);
  or or_3 (O2, and_3_out, and_7_out);
  or or_4 (O3, and_4_out, and_8_out);

  // Notes on the sheet:
  //   MUX
endmodule

module Register_File (
  input  A0,
  input  A1,
  input  A2,
  input  A3,
  input  WE,
  input  in_6,
  input  S0,
  output out_8,
  output out_9,
  output out_10,
  output out_11,
  output out_12,
  output out_13,
  output out_14,
  output out_15
);

  wire and_1_out, and_2_out, not_1_out;

  not not_1 (not_1_out, S0);
  and and_1 (and_1_out, WE, not_1_out);
  and and_2 (and_2_out, WE, S0);
  _4_Bit_Register u_4_bit_register_1 (
    .A0(A0), .A1(A1), .A2(A2), .A3(A3), .Clock(in_6), .Load(and_1_out), .out_7(out_8), .out_8(out_9),
    .out_9(out_10), .out_10(out_11));
  _4_Bit_Register u_4_bit_register_2 (
    .A0(A0), .A1(A1), .A2(A2), .A3(A3), .Clock(in_6), .Load(and_2_out), .out_7(out_12), .out_8(out_13),
    .out_9(out_14), .out_10(out_15));

  // Notes on the sheet:
  //   Register File
  //   Clock
endmodule

module _4_Bit_Register (
  input  A0,
  input  A1,
  input  A2,
  input  A3,
  input  Clock,
  input  Load,
  output out_7,
  output out_8,
  output out_9,
  output out_10
);

  // _1BitRegister 1bitregister_1: pin names not known; wires that end beside it: Clock, A0, Load, out_7
  // _1BitRegister 1bitregister_2: pin names not known; wires that end beside it: Clock, A1, Load, out_8
  // _1BitRegister 1bitregister_3: pin names not known; wires that end beside it: Clock, A2, Load, out_9
  // _1BitRegister 1bitregister_4: pin names not known; wires that end beside it: Clock, A3, Load, out_10

  // Notes on the sheet:
  //   4-Bit-Register
endmodule

module _1_Bit_Register (
  input  Clock,
  input  In,
  input  Load,
  output Out
);

  wire n2_1_mux_1_out;

  _2_1_MUX u_2_1_mux_1 (.In0(Out), .In1(In), .Load(Load), .Out(n2_1_mux_1_out));
  D_Flip_Flop d_ff_1 (.clk(Clock), .D(n2_1_mux_1_out), .Q(Out));  // open: Qn, preset, en, reset

  // Notes on the sheet:
  //   1-Bit-Register
endmodule

module _2_1_MUX (
  input  In0,
  input  In1,
  input  Load,
  output Out
);

  wire and_1_out, and_2_out, not_1_out;

  not not_1 (not_1_out, Load);
  and and_1 (and_1_out, In0, not_1_out);
  and and_2 (and_2_out, In1, Load);
  or or_1 (Out, and_1_out, and_2_out);

  // Notes on the sheet:
  //   2:1 MUX
endmodule

module _1_Bit_Full_Adder (
  input  in_1,
  input  in_2,
  input  in_3,
  output out_4
);

  wire multiplexer_1_out;

  Multiplexer #(.enable("false")) multiplexer_1 (.in0(out_4), .in1(in_2), .out(multiplexer_1_out), .sel(in_3));
  D_Flip_Flop d_ff_1 (.clk(in_1), .D(multiplexer_1_out), .Q(out_4));  // open: Qn, preset, en, reset

  // Notes on the sheet:
  //   1-Bit Full Adder
endmodule

module _4_Bit_Add_Sub (
  input  in_1,
  input  A0,
  input  A1,
  input  A2,
  input  A3,
  input  B0,
  input  B1,
  input  B2,
  input  B3,
  output OUT_0,
  output OUT_1,
  output OUT_2,
  output OUT_3
);

  wire fulladder1bit_1_p5, fulladder1bit_2_p5, fulladder1bit_3_p5, xor_1_out, xor_2_out, xor_3_out, xor_4_out;

  xor xor_1 (xor_1_out, in_1, B0);
  xor xor_2 (xor_2_out, in_1, B1);
  xor xor_3 (xor_3_out, in_1, B2);
  xor xor_4 (xor_4_out, in_1, B3);
  // fullAdder1Bit fulladder1bit_1: pin names not known; wires that end beside it: A0, xor_1_out, in_1, OUT_0, fulladder1bit_1_p5
  // fullAdder1Bit fulladder1bit_2: pin names not known; wires that end beside it: A1, xor_2_out, fulladder1bit_1_p5, OUT_1, fulladder1bit_2_p5
  // fullAdder1Bit fulladder1bit_3: pin names not known; wires that end beside it: A2, xor_3_out, fulladder1bit_2_p5, OUT_2, fulladder1bit_3_p5
  // fullAdder1Bit fulladder1bit_4: pin names not known; wires that end beside it: A3, xor_4_out, fulladder1bit_3_p5, OUT_3, 1'b0

  // Notes on the sheet:
  //   4-Bit Add/Sub
  //   C
endmodule
